// Logisim project Project1.circ as structural Verilog: 7 circuits, main circuit main
module main (
  input  in_1,
  input  Zero
);

  wire ALUSrc, Clk, MemRead, MemtoReg, MemWrite, PCSrc, RegDst, RegWrite;
  wire [1:0] ALUCtr_1_0, ExtOp_1_0;
  wire [4:0] Instr_20_16, Instr_25_21, multiplexer_1_out;
  wire [5:0] Instr_5_0, Instr_31_26;
  wire [15:6] Instr_15_0;
  wire [31:0] ALUResult, Ext32, multiplexer_2_out, multiplexer_3_out, ram_1_data, regfile_1_output1,
       regfile_1_output2;

  Clock clock_1 (.out(Clk));
  IFU ifu_1 (
    .IfBeq(PCSrc), .Zero(PCSrc), .clk(Clk), .Reset(in_1),
    .Instr({Instr_31_26, Instr_25_21, Instr_20_16, Instr_15_0, Instr_5_0}));  // open: PCAddress
  Multiplexer #(.width(5)) multiplexer_1 (
    .in0(Instr_20_16), .in1(Instr_15_0[15:11]), .out(multiplexer_1_out), .sel(RegDst));  // open: en
  Extender extender_1 (.Imm16({Instr_15_0, Instr_5_0}), .ExtOp_1_0(ExtOp_1_0), .ext32(Ext32));
  RegFile regfile_1 (
    .clk(Clk), .RegWrite(RegWrite), .A1(Instr_25_21), .A2(Instr_20_16), .A3(multiplexer_1_out),
    .Data(multiplexer_3_out), .Output1(regfile_1_output1), .Output2(regfile_1_output2));
  Controller controller_1 (
    .func(Instr_5_0), .opcode(Instr_31_26), .RegDst(RegDst), .ALUSrc(ALUSrc), .MemtoReg(MemtoReg),
    .RegWrite(RegWrite), .Memread(MemRead), .MemWrite(MemWrite), .PCSrc(PCSrc), .ALUCtr_1_0(ALUCtr_1_0),
    .ExtOp_1_0(ExtOp_1_0));
  Multiplexer #(.width(32)) multiplexer_2 (
    .in0(regfile_1_output2), .in1(Ext32), .out(multiplexer_2_out), .sel(ALUSrc));  // open: en
  ALU alu_1 (.X(regfile_1_output1), .Y(multiplexer_2_out), .ALUCtr_1_0(ALUCtr_1_0), .Result(ALUResult), .Zero(Zero));
  RAM #(.addrWidth(5), .dataWidth(32), .bus("separate")) ram_1 (
    .addr(ALUResult[4:0]), .din(regfile_1_output2), .data(ram_1_data), .str(MemWrite), .clk(Clk), .ld(MemRead));  // open: sel, clr
  Multiplexer #(.width(32)) multiplexer_3 (
    .in0(ALUResult), .in1(ram_1_data), .out(multiplexer_3_out), .sel(MemtoReg));  // open: en

  // Other names for the same wires on the sheet: Instr_15_0[5:0] = Instr_5_0; Instr_15_11[4:0] = Instr_15_0[15:11];
  //   Reset = in_1; Zero_t = PCSrc
endmodule

// GPR
module RegFile (
  input  clk,
  input  RegWrite,
  input  [4:0] A1,
  input  [4:0] A2,
  input  [4:0] A3,
  input  [31:0] Data,
  output [31:0] Output1,
  output [31:0] Output2
);

  wire demultiplexer_1_out0, demultiplexer_1_out1, demultiplexer_1_out2, demultiplexer_1_out3,
       demultiplexer_1_out4, demultiplexer_1_out5, demultiplexer_1_out6, demultiplexer_1_out7,
       demultiplexer_1_out8, demultiplexer_1_out9, demultiplexer_1_out10, demultiplexer_1_out11,
       demultiplexer_1_out12, demultiplexer_1_out13, demultiplexer_1_out14, demultiplexer_1_out15,
       demultiplexer_1_out16, demultiplexer_1_out17, demultiplexer_1_out18, demultiplexer_1_out19,
       demultiplexer_1_out20, demultiplexer_1_out21, demultiplexer_1_out22, demultiplexer_1_out23,
       demultiplexer_1_out24, demultiplexer_1_out25, demultiplexer_1_out26, demultiplexer_1_out27,
       demultiplexer_1_out28, demultiplexer_1_out29, demultiplexer_1_out30, demultiplexer_1_out31;
  wire [31:0] _0, _1, _2, _3, _4, _5, _6, _7, _8, _9, _10, _11, _12, _13, _14, _15, _16, _17, _18, _19, _20,
       _21, _22, _23, _24, _25, _26, _27, _28, _29, _30, _31;

  Demultiplexer #(.select(5)) demultiplexer_1 (
    .out0(demultiplexer_1_out0), .out1(demultiplexer_1_out1), .out2(demultiplexer_1_out2),
    .out3(demultiplexer_1_out3), .out4(demultiplexer_1_out4), .out5(demultiplexer_1_out5),
    .out6(demultiplexer_1_out6), .out7(demultiplexer_1_out7), .out8(demultiplexer_1_out8),
    .out9(demultiplexer_1_out9), .out10(demultiplexer_1_out10), .out11(demultiplexer_1_out11),
    .out12(demultiplexer_1_out12), .out13(demultiplexer_1_out13), .out14(demultiplexer_1_out14),
    .out15(demultiplexer_1_out15), .out16(demultiplexer_1_out16), .out17(demultiplexer_1_out17),
    .out18(demultiplexer_1_out18), .out19(demultiplexer_1_out19), .out20(demultiplexer_1_out20),
    .out21(demultiplexer_1_out21), .out22(demultiplexer_1_out22), .out23(demultiplexer_1_out23),
    .out24(demultiplexer_1_out24), .out25(demultiplexer_1_out25), .out26(demultiplexer_1_out26),
    .out27(demultiplexer_1_out27), .out28(demultiplexer_1_out28), .out29(demultiplexer_1_out29),
    .out30(demultiplexer_1_out30), .out31(demultiplexer_1_out31), .in(RegWrite), .sel(A3));  // open: en
  Register #(.width(32)) register_1 (.D(Data), .en(demultiplexer_1_out0), .Q(_0), .clk(clk));  // open: clr
  Register #(.width(32)) register_2 (.D(Data), .en(demultiplexer_1_out1), .Q(_1), .clk(clk));  // open: clr
  Register #(.width(32)) register_3 (.D(Data), .en(demultiplexer_1_out2), .Q(_2), .clk(clk));  // open: clr
  Register #(.width(32)) register_4 (.D(Data), .en(demultiplexer_1_out3), .Q(_3), .clk(clk));  // open: clr
  Register #(.width(32)) register_5 (.D(Data), .en(demultiplexer_1_out4), .Q(_4), .clk(clk));  // open: clr
  Register #(.width(32)) register_6 (.D(Data), .en(demultiplexer_1_out5), .Q(_5), .clk(clk));  // open: clr
  Register #(.width(32)) register_7 (.D(Data), .en(demultiplexer_1_out6), .Q(_6), .clk(clk));  // open: clr
  Register #(.width(32)) register_8 (.D(Data), .en(demultiplexer_1_out7), .Q(_7), .clk(clk));  // open: clr
  Register #(.width(32)) register_9 (.D(Data), .en(demultiplexer_1_out8), .Q(_8), .clk(clk));  // open: clr
  Register #(.width(32)) register_10 (.D(Data), .en(demultiplexer_1_out9), .Q(_9), .clk(clk));  // open: clr
  Register #(.width(32)) register_11 (.D(Data), .en(demultiplexer_1_out10), .Q(_10), .clk(clk));  // open: clr
  Register #(.width(32)) register_12 (.D(Data), .en(demultiplexer_1_out11), .Q(_11), .clk(clk));  // open: clr
  Register #(.width(32)) register_13 (.D(Data), .en(demultiplexer_1_out12), .Q(_12), .clk(clk));  // open: clr
  Register #(.width(32)) register_14 (.D(Data), .en(demultiplexer_1_out13), .Q(_13), .clk(clk));  // open: clr
  Register #(.width(32)) register_15 (.D(Data), .en(demultiplexer_1_out14), .Q(_14), .clk(clk));  // open: clr
  Register #(.width(32)) register_16 (.D(Data), .en(demultiplexer_1_out15), .Q(_15), .clk(clk));  // open: clr
  Register #(.width(32)) register_17 (.D(Data), .en(demultiplexer_1_out16), .Q(_16), .clk(clk));  // open: clr
  Register #(.width(32)) register_18 (.D(Data), .en(demultiplexer_1_out17), .Q(_17), .clk(clk));  // open: clr
  Register #(.width(32)) register_19 (.D(Data), .en(demultiplexer_1_out18), .Q(_18), .clk(clk));  // open: clr
  Register #(.width(32)) register_20 (.D(Data), .en(demultiplexer_1_out19), .Q(_19), .clk(clk));  // open: clr
  Register #(.width(32)) register_21 (.D(Data), .en(demultiplexer_1_out20), .Q(_20), .clk(clk));  // open: clr
  Register #(.width(32)) register_22 (.D(Data), .en(demultiplexer_1_out21), .Q(_21), .clk(clk));  // open: clr
  Register #(.width(32)) register_23 (.D(Data), .en(demultiplexer_1_out22), .Q(_22), .clk(clk));  // open: clr
  Register #(.width(32)) register_24 (.D(Data), .en(demultiplexer_1_out23), .Q(_23), .clk(clk));  // open: clr
  Register #(.width(32)) register_25 (.D(Data), .en(demultiplexer_1_out24), .Q(_24), .clk(clk));  // open: clr
  Register #(.width(32)) register_26 (.D(Data), .en(demultiplexer_1_out25), .Q(_25), .clk(clk));  // open: clr
  Register #(.width(32)) register_27 (.D(Data), .en(demultiplexer_1_out26), .Q(_26), .clk(clk));  // open: clr
  Register #(.width(32)) register_28 (.D(Data), .en(demultiplexer_1_out27), .Q(_27), .clk(clk));  // open: clr
  Register #(.width(32)) register_29 (.D(Data), .en(demultiplexer_1_out28), .Q(_28), .clk(clk));  // open: clr
  Register #(.width(32)) register_30 (.D(Data), .en(demultiplexer_1_out29), .Q(_29), .clk(clk));  // open: clr
  Register #(.width(32)) register_31 (.D(Data), .en(demultiplexer_1_out30), .Q(_30), .clk(clk));  // open: clr
  Register #(.width(32)) register_32 (.D(Data), .en(demultiplexer_1_out31), .Q(_31), .clk(clk));  // open: clr
  Multiplexer #(.select(5), .width(32)) multiplexer_1 (
    .in0(_0), .in1(_1), .in2(_2), .in3(_3), .in4(_4), .in5(_5), .in6(_6), .in7(_7), .in8(_8), .in9(_9),
    .in10(_10), .in11(_11), .in12(_12), .in13(_13), .in14(_14), .in15(_15), .in16(_16), .in17(_17),
    .in18(_18), .in19(_19), .in20(_20), .in21(_21), .in22(_22), .in23(_23), .in24(_24), .in25(_25),
    .in26(_26), .in27(_27), .in28(_28), .in29(_29), .in30(_30), .in31(_31), .out(Output1), .sel(A1));  // open: en
  Multiplexer #(.select(5), .width(32)) multiplexer_2 (
    .in0(_0), .in1(_1), .in2(_2), .in3(_3), .in4(_4), .in5(_5), .in6(_6), .in7(_7), .in8(_8), .in9(_9),
    .in10(_10), .in11(_11), .in12(_12), .in13(_13), .in14(_14), .in15(_15), .in16(_16), .in17(_17),
    .in18(_18), .in19(_19), .in20(_20), .in21(_21), .in22(_22), .in23(_23), .in24(_24), .in25(_25),
    .in26(_26), .in27(_27), .in28(_28), .in29(_29), .in30(_30), .in31(_31), .out(Output2), .sel(A2));  // open: en

  // Other names for the same wires on the sheet: A1Ctr[4:0] = A1; A2Ctr[4:0] = A2; A3Ctr[4:0] = A3
endmodule

module ALU (
  input  [31:0] X,
  input  [31:0] Y,
  input  [1:0] ALUCtr_1_0,
  output Zero,
  output [31:0] Result
);

  wire [31:0] adder_1_out, orer_1_result, subtractor_1_out;

  Adder #(.width(32)) adder_1 (.a(X), .b(Y), .out(adder_1_out));  // open: cin, cout
  Subtractor #(.width(32)) subtractor_1 (.a(X), .b(Y), .out(subtractor_1_out));  // open: bin, bout
  Orer orer_1 (.X(X), .Y(Y), .Result(orer_1_result));
  Multiplexer #(.select(2), .width(32)) multiplexer_1 (
    .in0(adder_1_out), .in1(subtractor_1_out), .in2(orer_1_result), .out(Result), .sel(ALUCtr_1_0));  // open: in3, en
  Comparator #(.width(32)) comparator_1 (.a(Result), .b({32{1'b0}}), .eq(Zero));  // open: gt, lt
endmodule

module Controller (
  input  [5:0] func,
  input  [5:0] opcode,
  output RegDst,
  output ALUSrc,
  output MemtoReg,
  output RegWrite,
  output Memread,
  output MemWrite,
  output PCSrc,
  output [1:0] ALUCtr_1_0,
  output [1:0] ExtOp_1_0
);

  wire addu_out, beq_out, lui_out, lw_out, not_1_out, not_2_out, not_3_out, not_4_out, not_5_out, not_6_out,
       not_7_out, not_8_out, not_9_out, not_10_out, not_11_out, not_12_out, ori_out, subu_out, sw_out;

  not not_1 (not_1_out, func[5]);
  not not_2 (not_2_out, func[4]);
  not not_3 (not_3_out, func[3]);
  not not_4 (not_4_out, func[2]);
  not not_5 (not_5_out, func[1]);
  not not_6 (not_6_out, func[0]);
  not not_7 (not_7_out, opcode[5]);
  not not_8 (not_8_out, opcode[4]);
  not not_9 (not_9_out, opcode[3]);
  not not_10 (not_10_out, opcode[2]);
  not not_11 (not_11_out, opcode[1]);
  not not_12 (not_12_out, opcode[0]);
  and addu (addu_out, func[5], not_2_out, not_3_out, not_4_out, not_5_out, func[0], not_7_out, not_8_out, not_9_out, not_10_out, not_11_out, not_12_out);
  and subu (subu_out, func[5], not_2_out, not_3_out, not_4_out, func[1], func[0], not_7_out, not_8_out, not_9_out, not_10_out, not_11_out, not_12_out);
  and ori (ori_out, not_7_out, not_8_out, opcode[3], opcode[2], not_11_out, opcode[0]);
  and lw (lw_out, opcode[5], not_8_out, not_9_out, not_10_out, opcode[1], opcode[0]);
  and sw (sw_out, opcode[5], not_8_out, opcode[3], not_10_out, opcode[1], opcode[0]);
  and beq (beq_out, not_7_out, not_8_out, not_9_out, opcode[2], not_11_out, not_12_out);
  and lui (lui_out, not_7_out, not_8_out, opcode[3], opcode[2], opcode[1], opcode[0]);
  or u_RegDst (RegDst, addu_out, subu_out);
  or u_ALUSrc (ALUSrc, ori_out, lw_out, sw_out, lui_out);
  buf u_MemtoReg (MemtoReg, lw_out);  // OR_Gate
  or u_RegWrite (RegWrite, addu_out, subu_out, lui_out, ori_out, lw_out);
  buf u_Memread (Memread, lw_out);  // OR_Gate
  buf u_MemWrite (MemWrite, sw_out);  // OR_Gate
  buf u_PCSrc (PCSrc, beq_out);  // OR_Gate
  buf ALUCtr1 (ALUCtr_1_0[1], ori_out);  // OR_Gate
  or ALUCtr0 (ALUCtr_1_0[0], subu_out, beq_out);
  buf ExtOp_1 (ExtOp_1_0[1], lui_out);  // OR_Gate
  or ExtOp_0 (ExtOp_1_0[0], lw_out, sw_out);

  // Notes on the sheet:
  //   0
  //   1
  //   1
  //   0
endmodule

module IFU (
  input  IfBeq,
  input  Zero,
  input  clk,
  input  Reset,
  output [4:0] PCAddress,
  output [31:0] Instr
);

  wire and_1_out;
  wire [29:5] PC_q;
  wire [31:0] adder_1_out, adder_2_out, bit_extender_1_out, multiplexer_1_out, shifter_1_out;

  Register #(.width(30)) PC (.D(multiplexer_1_out[29:0]), .Q({PC_q, PCAddress}), .clk(clk), .clr(Reset));  // open: en
  ROM #(.addrWidth(5), .dataWidth(32)) rom_1 (.addr(PCAddress), .data(Instr));  // open: sel
  Adder #(.width(32)) adder_1 (.a({2'b00, PC_q, PCAddress}), .b(32'h1), .out(adder_1_out));  // open: cin, cout
  assign bit_extender_1_out = {{16{1'b0}}, Instr[15:0]};  // Bit_Extender bit_extender_1
  Shifter #(.width(32)) shifter_1 (.in(bit_extender_1_out), .\dist (5'b00010), .out(shifter_1_out));
  Adder #(.width(32)) adder_2 (.a(adder_1_out), .b(shifter_1_out), .out(adder_2_out));  // open: cin, cout
  Multiplexer #(.width(32)) multiplexer_1 (
    .in0(adder_1_out), .in1(adder_2_out), .out(multiplexer_1_out), .sel(and_1_out));  // open: en
  and and_1 (and_1_out, IfBeq, Zero);

  // Notes on the sheet:
  //   contents of rom_1 (hex, n*v repeats v):
  //   3c0800ff 3c090001 1095021 1495023 350b5555 3c0c0001 3c0d0001 35ad0001 1ac6023 1ec4021 1084021
  //   1084021 1ef4821 18c6821 1ad6821 1ac7021 1cc7821 12c4821 11090000 3c081001 ad0f0000 8d0d0000
endmodule

// Ext
module Extender (
  input  [15:0] Imm16,
  input  [1:0] ExtOp_1_0,
  output [31:0] ext32
);

  wire [31:0] bit_extender_1_out, bit_extender_2_out;

  assign bit_extender_1_out = {{16{1'b0}}, Imm16};  // Bit_Extender bit_extender_1
  assign bit_extender_2_out = {{16{Imm16[15]}}, Imm16};  // Bit_Extender bit_extender_2
  Multiplexer #(.select(2), .width(32)) multiplexer_1 (
    .in0(bit_extender_1_out), .in1(bit_extender_2_out), .in2({Imm16, {16{1'b0}}}), .out(ext32),
    .sel(ExtOp_1_0));  // open: in3, en

  // Notes on the sheet:
  //   低16位补0
  //   lui 拓展到高16位
endmodule

module Orer (
  input  [31:0] X,
  input  [31:0] Y,
  output [31:0] Result
);

  assign Result = X | Y;  // OR_Gate or_1, 32 bits wide
endmodule
